// Logisim project 单周期mips.circ as structural Verilog: 29 circuits, main circuit adder_1
module adder_1 (
  input  C,
  input  A,
  input  B,
  output S,
  output C_1
);

  wire and_1_out, and_2_out, or_1_out, xor_1_out;

  or or_1 (or_1_out, B, A);
  and and_1 (and_1_out, B, A);
  and and_2 (and_2_out, or_1_out, C);
  xor xor_1 (xor_1_out, A, B);
  xor xor_2 (S, C, xor_1_out);
  or or_2 (C_1, and_1_out, and_2_out);
endmodule

module adder_4 (
  input  C_i_1,
  input  xi_0,
  input  xi_1,
  input  xi_2,
  input  xi_3,
  input  yi_0,
  input  yi_1,
  input  yi_2,
  input  yi_3,
  output out_10,
  output out_11,
  output out_12,
  output out_13,
  output C
);

  wire adder_1_1_c_1, adder_1_2_c_1, adder_1_3_c_1;

  adder_1 adder_1_1 (.C(xi_0), .A(yi_0), .B(C_i_1), .S(out_10), .C_1(adder_1_1_c_1));
  adder_1 adder_1_2 (.C(adder_1_1_c_1), .A(xi_1), .B(yi_1), .S(out_11), .C_1(adder_1_2_c_1));
  adder_1 adder_1_3 (.C(adder_1_2_c_1), .A(xi_2), .B(yi_2), .S(out_12), .C_1(adder_1_3_c_1));
  adder_1 adder_1_4 (.C(adder_1_3_c_1), .A(xi_3), .B(yi_3), .S(out_13), .C_1(C));
endmodule

module adder_8 (
  input  C_i_1,
  input  xi_0,
  input  xi_1,
  input  xi_2,
  input  xi_3,
  input  in_6,
  input  in_7,
  input  in_8,
  input  in_9,
  input  in_10,
  input  in_11,
  input  in_12,
  input  in_13,
  input  in_14,
  input  in_15,
  input  in_16,
  input  in_17,
  output out_18,
  output out_19,
  output out_20,
  output out_21,
  output out_22,
  output out_23,
  output out_24,
  output out_25,
  output out_26
);

  wire adder_4_1_c;

  adder_4 adder_4_1 (
    .C_i_1(C_i_1), .xi_0(xi_0), .xi_1(xi_1), .xi_2(xi_2), .xi_3(xi_3), .yi_0(in_10), .yi_1(in_11),
    .yi_2(in_12), .yi_3(in_13), .out_10(out_18), .out_11(out_19), .out_12(out_20), .out_13(out_21),
    .C(adder_4_1_c));
  adder_4 adder_4_2 (
    .C_i_1(adder_4_1_c), .xi_0(in_6), .xi_1(in_7), .xi_2(in_8), .xi_3(in_9), .yi_0(in_14), .yi_1(in_15),
    .yi_2(in_16), .yi_3(in_17), .out_10(out_22), .out_11(out_23), .out_12(out_24), .out_13(out_25), .C(out_26));
endmodule

module adder_16 (
  input  in_1,
  input  [15:0] in_2,
  input  [15:0] in_3,
  output [15:0] out_4,
  output out_5
);

  wire adder_8_1_out_26;

  adder_8 adder_8_1 (
    .C_i_1(in_1), .xi_0(in_2[0]), .xi_1(in_2[1]), .xi_2(in_2[2]), .xi_3(in_2[3]), .in_6(in_2[4]),
    .in_7(in_2[5]), .in_8(in_2[6]), .in_9(in_2[7]), .in_10(in_3[0]), .in_11(in_3[1]), .in_12(in_3[2]),
    .in_13(in_3[3]), .in_14(in_3[4]), .in_15(in_3[5]), .in_16(in_3[6]), .in_17(in_3[7]), .out_18(out_4[0]),
    .out_19(out_4[1]), .out_20(out_4[2]), .out_21(out_4[3]), .out_22(out_4[4]), .out_23(out_4[5]),
    .out_24(out_4[6]), .out_25(out_4[7]), .out_26(adder_8_1_out_26));
  adder_8 adder_8_2 (
    .C_i_1(adder_8_1_out_26), .xi_0(in_2[8]), .xi_1(in_2[9]), .xi_2(in_2[10]), .xi_3(in_2[11]),
    .in_6(in_2[12]), .in_7(in_2[13]), .in_8(in_2[14]), .in_9(in_2[15]), .in_10(in_3[8]), .in_11(in_3[9]),
    .in_12(in_3[10]), .in_13(in_3[11]), .in_14(in_3[12]), .in_15(in_3[13]), .in_16(in_3[14]),
    .in_17(in_3[15]), .out_18(out_4[8]), .out_19(out_4[9]), .out_20(out_4[10]), .out_21(out_4[11]),
    .out_22(out_4[12]), .out_23(out_4[13]), .out_24(out_4[14]), .out_25(out_4[15]), .out_26(out_5));

  // Notes on the sheet:
  //   in_3: initial=0xf2
  //   in_2: initial=0xf2
endmodule

module adder_32 (
  input  in_1,
  input  [31:0] in_2,
  input  [31:0] in_3,
  output [31:0] out_4,
  output out_5
);

  wire adder_16_1_out_5;

  adder_16 adder_16_1 (
    .in_1(in_1), .in_2(in_2[15:0]), .in_3(in_3[15:0]), .out_4(out_4[15:0]), .out_5(adder_16_1_out_5));
  adder_16 adder_16_2 (
    .in_1(adder_16_1_out_5), .in_2(in_2[31:16]), .in_3(in_3[31:16]), .out_4(out_4[31:16]), .out_5(out_5));

  // Notes on the sheet:
  //   in_2: initial=0x12345678
  //   in_3: initial=0xf1249649
endmodule

module sub_32 (
  input  [31:0] in_1,
  input  [31:0] in_2,
  output [31:0] out_3
);

  wire adder_32_1_out_5;
  wire [31:0] not_1_out;

  assign not_1_out = ~in_2;  // NOT_Gate not_1, 32 bits wide
  adder_32 adder_32_1 (.in_1(1'b1), .in_2(in_1), .in_3(not_1_out), .out_4(out_3), .out_5(adder_32_1_out_5));
  // NoConnect on adder_32_1_out_5

  // Notes on the sheet:
  //   in_2: initial=0x40
endmodule

module CPU (
  input  reset
);

  wire clock_1_out, controller_1_alusrc, controller_1_beq, controller_1_extop, controller_1_mem2reg,
       controller_1_memwrite, controller_1_regdst, controller_1_regwrite, iszero_1_out_2;
  wire [1:0] controller_1_aluop;
  wire [4:0] alu_1_output_result_2, multiplexer_1_out;
  wire [31:0] alu_1_output_result, ext_1_out_data_32, ifu_1_output_instruction, multiplexer_2_out,
       multiplexer_3_out, ram_1_dout, reg_file_output_read_data_0, reg_file_output_read_data_1;

  Clock clock_1 (.out(clock_1_out));
  IsZero iszero_1 (
    .in_1({alu_1_output_result[31:7], alu_1_output_result_2, alu_1_output_result[1:0]}),
    .out_2(iszero_1_out_2));
  IFU ifu_1 (
    .ifbeq(controller_1_beq), .zero(iszero_1_out_2), .clock(clock_1_out), .reset(reset),
    .output_instruction(ifu_1_output_instruction));
  Multiplexer #(.width(5)) multiplexer_1 (
    .in0(ifu_1_output_instruction[20:16]), .in1(ifu_1_output_instruction[15:11]), .out(multiplexer_1_out),
    .sel(controller_1_regdst));
  Controller controller_1 (
    .Opcode(ifu_1_output_instruction[31:26]), .Func(ifu_1_output_instruction[5:0]),
    .Regdst(controller_1_regdst), .Alusrc(controller_1_alusrc), .Mem2reg(controller_1_mem2reg),
    .Regwrite(controller_1_regwrite), .Memwrite(controller_1_memwrite), .beq(controller_1_beq),
    .extop(controller_1_extop), .Aluop(controller_1_aluop));
  reg32 reg_file (
    .input_data(multiplexer_3_out), .read_or_write(controller_1_regwrite), .clock(clock_1_out),
    .reset(reset), .read_0_5(ifu_1_output_instruction[25:21]), .read_1_5(ifu_1_output_instruction[20:16]),
    .write_0_5(multiplexer_1_out), .output_read_data_0(reg_file_output_read_data_0),
    .output_read_data_1(reg_file_output_read_data_1));
  EXT ext_1 (
    .input_data_16(ifu_1_output_instruction[15:0]), .control(controller_1_extop),
    .out_data_32(ext_1_out_data_32));
  Multiplexer #(.width(32)) multiplexer_2 (
    .in0(reg_file_output_read_data_1), .in1(ext_1_out_data_32), .out(multiplexer_2_out),
    .sel(controller_1_alusrc));
  Multiplexer #(.width(32)) multiplexer_3 (
    .in0({alu_1_output_result[31:7], alu_1_output_result_2, alu_1_output_result[1:0]}), .in1(ram_1_dout),
    .out(multiplexer_3_out), .sel(controller_1_mem2reg));
  ALU alu_1 (
    .input_value_0(reg_file_output_read_data_0), .input_value_1(multiplexer_2_out), .F(controller_1_aluop),
    .output_result({alu_1_output_result[31:7], alu_1_output_result_2, alu_1_output_result[1:0]}));
  RAM #(.addrWidth(5), .asyncread("true"), .clearpin("true"), .dataWidth(32), .trigger("falling")) ram_1 (
    .addr(alu_1_output_result_2), .we(controller_1_memwrite), .oe(controller_1_mem2reg), .clk(clock_1_out),
    .din(reg_file_output_read_data_1), .dout(ram_1_dout), .clr(reset));

  // Notes on the sheet:
  //   2.此处的EXT只有高位补0还是低位补0
  //   1. lw  和 sw的 reg + offset不支持offset为负数(有符号拓展)
  //   16 imm
  //   imm 16
  //   rs
  //   rt
  //   rd
  //   Use reg dst
  //   这里一个地址对应一个字节
  //   DM 一个地址对应4个字节
endmodule

module ALU (
  input  [31:0] input_value_0,
  input  [31:0] input_value_1,
  input  [1:0] F,
  output [31:0] output_result
);

  wire adder_32_1_out_5, not_2_out;
  wire [31:0] adder_32_1_out_4, multiplexer_1_out, not_1_out, or_1_out;

  // NoConnect on F[1]
  assign not_1_out = ~input_value_1;  // NOT_Gate not_1, 32 bits wide
  Multiplexer #(.width(32)) multiplexer_1 (.in0(not_1_out), .in1(input_value_1), .out(multiplexer_1_out), .sel(F[0]));
  not not_2 (not_2_out, F[0]);
  assign or_1_out = input_value_0 | multiplexer_1_out;  // OR_Gate or_1, 32 bits wide
  adder_32 adder_32_1 (
    .in_1(not_2_out), .in_2(input_value_0), .in_3(multiplexer_1_out), .out_4(adder_32_1_out_4),
    .out_5(adder_32_1_out_5));
  // NoConnect on adder_32_1_out_5
  Multiplexer #(.select(2), .width(32)) multiplexer_2 (
    .in1(or_1_out), .in2(adder_32_1_out_4), .in3(adder_32_1_out_4), .out(output_result), .sel(F));  // open: in0

  // Notes on the sheet:
  //   F: initial=0x3
  //   or__00
  //   sub_01
  //   add_10
endmodule

module reg_4_old (
  input  [31:0] in_1,
  input  read_or_write,
  input  clock,
  input  reset,
  input  [1:0] read_0,
  input  [1:0] read_1,
  input  [1:0] write_0,
  output [31:0] out_8,
  output [31:0] out_9
);

  wire [31:0] multiplexer_1_out, multiplexer_2_out, multiplexer_3_out, multiplexer_4_out, multiplexer_5_out,
       multiplexer_6_out, register_1_q, register_2_q, register_3_q, register_4_q;

  Multiplexer #(.width(32)) multiplexer_1 (
    .in0(multiplexer_2_out), .in1(in_1), .out(multiplexer_1_out), .sel(read_or_write));
  Multiplexer #(.select(2), .width(32)) multiplexer_2 (
    .in0(register_1_q), .in1(register_2_q), .in2(register_3_q), .in3(register_4_q), .out(multiplexer_2_out),
    .sel(write_0));
  Multiplexer #(.select(2), .width(32)) multiplexer_3 (
    .in0(multiplexer_1_out), .in1(register_1_q), .in2(register_1_q), .in3(register_1_q),
    .out(multiplexer_3_out), .sel(write_0));
  Multiplexer #(.select(2), .width(32)) multiplexer_4 (
    .in0(register_2_q), .in1(multiplexer_1_out), .in2(register_2_q), .in3(register_2_q),
    .out(multiplexer_4_out), .sel(write_0));
  Multiplexer #(.select(2), .width(32)) multiplexer_5 (
    .in0(register_3_q), .in1(register_3_q), .in2(multiplexer_1_out), .in3(register_3_q),
    .out(multiplexer_5_out), .sel(write_0));
  Multiplexer #(.select(2), .width(32)) multiplexer_6 (
    .in0(register_4_q), .in1(register_4_q), .in2(register_4_q), .in3(multiplexer_1_out),
    .out(multiplexer_6_out), .sel(write_0));
  Register #(.width(32)) register_1 (.D(multiplexer_3_out), .clk(clock), .Q(register_1_q), .clr(reset));  // open: en
  Register #(.width(32)) register_2 (.D(multiplexer_4_out), .clk(clock), .Q(register_2_q), .clr(reset));  // open: en
  Register #(.width(32)) register_3 (.D(multiplexer_5_out), .clk(clock), .Q(register_3_q), .clr(reset));  // open: en
  Register #(.width(32)) register_4 (.D(multiplexer_6_out), .clk(clock), .Q(register_4_q), .clr(reset));  // open: en
  Multiplexer #(.select(2), .width(32)) multiplexer_7 (
    .in0(register_1_q), .in1(register_2_q), .in2(register_3_q), .in3(register_4_q), .out(out_8), .sel(read_0));
  Multiplexer #(.select(2), .width(32)) multiplexer_8 (
    .in0(register_1_q), .in1(register_2_q), .in2(register_3_q), .in3(register_4_q), .out(out_9), .sel(read_1));

  // Notes on the sheet:
  //   in_1: initial=0xffffffff
  //   out_0
  //   out_1
endmodule

module or_32 (
  input  [31:0] in_1,
  input  [31:0] in_2,
  output [31:0] out_3
);

  assign out_3 = in_1 | in_2;  // OR_Gate or_1, 32 bits wide
endmodule

module reg_8 (
  input  [31:0] in_1,
  input  read_or_write,
  input  clock,
  input  reset,
  input  [2:0] read_0,
  input  [2:0] read_1,
  input  [2:0] write_0,
  output [31:0] out_8,
  output [31:0] out_9
);

  wire [31:0] demultiplexer_1_out0, demultiplexer_1_out1, reg_4_1_out_0, reg_4_1_out_1, reg_4_2_out_0,
       reg_4_2_out_1;

  Demultiplexer #(.width(32)) demultiplexer_1 (
    .out0(demultiplexer_1_out0), .out1(demultiplexer_1_out1), .in(in_1), .sel(write_0[2]));
  reg_4 reg_4_1 (
    .in_1(demultiplexer_1_out0), .read_or_write(read_or_write), .clock(clock), .reset(reset),
    .read_0(read_0[1:0]), .read_1(read_1[1:0]), .write_0(write_0[1:0]), .out_0(reg_4_1_out_0),
    .out_1(reg_4_1_out_1));
  reg_4 reg_4_2 (
    .in_1(demultiplexer_1_out1), .read_or_write(read_or_write), .clock(clock), .reset(reset),
    .read_0(read_0[1:0]), .read_1(read_1[1:0]), .write_0(write_0[1:0]), .out_0(reg_4_2_out_0),
    .out_1(reg_4_2_out_1));
  Multiplexer #(.width(32)) multiplexer_1 (.in0(reg_4_1_out_0), .in1(reg_4_2_out_0), .out(out_8), .sel(read_0[2]));
  Multiplexer #(.width(32)) multiplexer_2 (.in0(reg_4_1_out_1), .in1(reg_4_2_out_1), .out(out_9), .sel(read_1[2]));

  // Notes on the sheet:
  //   in_1: initial=0xffffffff
endmodule

module reg16 (
  input  [31:0] in_1,
  input  read_or_write,
  input  clock,
  input  reset,
  input  [3:0] read_0,
  input  [3:0] read_1,
  input  [3:0] write_0,
  output [31:0] out_8,
  output [31:0] out_9
);

  wire [31:0] demultiplexer_1_out0, demultiplexer_1_out1, reg_8_1_out_8, reg_8_1_out_9, reg_8_2_out_8,
       reg_8_2_out_9;

  Demultiplexer #(.width(32)) demultiplexer_1 (
    .out0(demultiplexer_1_out0), .out1(demultiplexer_1_out1), .in(in_1), .sel(write_0[3]));
  reg_8 reg_8_1 (
    .in_1(demultiplexer_1_out0), .read_or_write(read_or_write), .clock(clock), .reset(reset),
    .read_0(read_0[2:0]), .read_1(read_1[2:0]), .write_0(write_0[2:0]), .out_8(reg_8_1_out_8),
    .out_9(reg_8_1_out_9));
  reg_8 reg_8_2 (
    .in_1(demultiplexer_1_out1), .read_or_write(read_or_write), .clock(clock), .reset(reset),
    .read_0(read_0[2:0]), .read_1(read_1[2:0]), .write_0(write_0[2:0]), .out_8(reg_8_2_out_8),
    .out_9(reg_8_2_out_9));
  Multiplexer #(.width(32)) multiplexer_1 (.in0(reg_8_1_out_8), .in1(reg_8_2_out_8), .out(out_8), .sel(read_0[3]));
  Multiplexer #(.width(32)) multiplexer_2 (.in0(reg_8_1_out_9), .in1(reg_8_2_out_9), .out(out_9), .sel(read_1[3]));

  // Notes on the sheet:
  //   in_1: initial=0xffffffff
endmodule

module reg32 (
  input  [31:0] input_data,
  input  read_or_write,
  input  clock,
  input  reset,
  input  [4:0] read_0_5,
  input  [4:0] read_1_5,
  input  [4:0] write_0_5,
  output [31:0] output_read_data_0,
  output [31:0] output_read_data_1
);

  wire [31:0] demultiplexer_1_out0, demultiplexer_1_out1, reg16_1_out_8, reg16_1_out_9, reg16_2_out_8,
       reg16_2_out_9;

  Demultiplexer #(.width(32)) demultiplexer_1 (
    .out0(demultiplexer_1_out0), .out1(demultiplexer_1_out1), .in(input_data), .sel(write_0_5[4]));
  reg16 reg16_1 (
    .in_1(demultiplexer_1_out0), .read_or_write(read_or_write), .clock(clock), .reset(reset),
    .read_0(read_0_5[3:0]), .read_1(read_1_5[3:0]), .write_0(write_0_5[3:0]), .out_8(reg16_1_out_8),
    .out_9(reg16_1_out_9));
  reg16 reg16_2 (
    .in_1(demultiplexer_1_out1), .read_or_write(read_or_write), .clock(clock), .reset(reset),
    .read_0(read_0_5[3:0]), .read_1(read_1_5[3:0]), .write_0(write_0_5[3:0]), .out_8(reg16_2_out_8),
    .out_9(reg16_2_out_9));
  Multiplexer #(.width(32)) multiplexer_1 (
    .in0(reg16_1_out_8), .in1(reg16_2_out_8), .out(output_read_data_0), .sel(read_0_5[4]));
  Multiplexer #(.width(32)) multiplexer_2 (
    .in0(reg16_1_out_9), .in1(reg16_2_out_9), .out(output_read_data_1), .sel(read_1_5[4]));

  // Notes on the sheet:
  //   input_data: initial=0xffffffff
endmodule

module EXT (
  input  [15:0] input_data_16,
  input  control,
  output [31:0] out_data_32
);

  Multiplexer #(.width(32)) multiplexer_1 (
    .in0({{16{1'b0}}, input_data_16}), .in1({input_data_16, {16{1'b0}}}), .out(out_data_32), .sel(control));

  // Notes on the sheet:
  //   input_data_16: initial=0xffff
endmodule

module IFU (
  input  ifbeq,
  input  zero,
  input  clock,
  input  reset,
  output [31:0] output_instruction
);

  wire adder_32_1_out_5, and_1_out;
  wire [1:0] multiplexer_1_out_2;
  wire [4:0] register_1_q;
  wire [29:0] multiplexer_1_out;
  wire [29:5] register_1_q_2;
  wire [31:0] adder_32_1_out_4, adder_32_2_out_4, ext_1_p3;

  // NoConnect on multiplexer_1_out_2
  Register #(.width(30)) register_1 (
    .D(multiplexer_1_out), .clk(clock), .Q({register_1_q_2, register_1_q}), .clr(reset));  // open: en
  Multiplexer #(.width(32)) multiplexer_1 (
    .in0(adder_32_1_out_4), .in1(adder_32_2_out_4), .out({multiplexer_1_out_2, multiplexer_1_out}),
    .sel(and_1_out));
  and and_1 (and_1_out, ifbeq, zero);
  adder_32 adder_32_1 (
    .in_1(1'b1), .in_2({32{1'b0}}), .in_3({2'b00, register_1_q_2, register_1_q}), .out_4(adder_32_1_out_4),
    .out_5(adder_32_1_out_5));
  // NoConnect on adder_32_1_out_5
  ROM #(.addrWidth(5), .dataWidth(32)) rom_1 (.addr(register_1_q), .data(output_instruction));
  // NoConnect on nothing
  // NoConnect on output_instruction[31:16]
  // EXT ext_1: pin names not known; wires that end beside it: output_instruction[15:0], 1'b0, ext_1_p3
  adder_32 adder_32_2 (.in_1(1'b0), .in_2(adder_32_1_out_4), .in_3(ext_1_p3), .out_4(adder_32_2_out_4));  // open: out_5

  // Notes on the sheet:
  //   PC
  //   这两个同时为True 才会add offset
  //   PC + 1
  //   contents of rom_1 (hex, n*v repeats v):
  //   34630010 ac030000 ac000004 ac000008 8c030000 10600017 8c020004 1821 3463000c 431021 8c030000
  //   ac430000 1821 34630004 8c020004 621021 ac020004 8c020000 1821 34630001 431023 ac020000 8c020000
  //   3c030001 621021 8c030008 621021 ac020008 1000ffe7
  //   忽略低16位
  //   高位补0
endmodule

module DM (
  input  [31:0] input_data,
  input  MemRead,
  input  MemWrite,
  input  Clock,
  input  Reset,
  input  [4:0] Address,
  output [31:0] out_data
);

  RAM #(.addrWidth(5), .clearpin("true"), .dataWidth(32), .trigger("falling")) ram_1 (
    .addr(Address), .we(MemWrite), .oe(MemRead), .clk(Clock), .din(input_data), .dout(out_data), .clr(Reset));
endmodule

module Controller (
  input  [5:0] Opcode,
  input  [5:0] Func,
  output Regdst,
  output Alusrc,
  output Mem2reg,
  output Regwrite,
  output Memwrite,
  output beq,
  output extop,
  output [1:0] Aluop
);

  RegDest_imp regdest_imp_1 (.opcode(Opcode), .func(Func), .out_3(Regdst));
  ALUSrc_imp alusrc_imp_1 (.opcode(Opcode), .out_2(Alusrc));
  Mem2Reg_imp mem2reg_imp_1 (.opcode(Opcode), .out_2(Mem2reg));
  RegWrite_imp regwrite_imp_1 (.Opcode(Opcode), .func(Func), .out_3(Regwrite));
  MemWrite_imp memwrite_imp_1 (.opcode(Opcode), .out_2(Memwrite));
  BEQ_imp beq_imp_1 (.opcode(Opcode), .out_2(beq));
  ExtOp_imp extop_imp_1 (.Opcode(Opcode), .out_2(extop));
  ALUCtr0_imp aluctr0_imp_1 (.Opcode(Opcode), .func(Func), .out_3(Aluop[0]));
  ALUCrt1_imp alucrt1_imp_1 (.Opcode(Opcode), .out_2(Aluop[1]));
endmodule

module RegDest_imp (
  input  [5:0] opcode,
  input  [5:0] func,
  output out_3
);

  wire [2:0] not_2_out;
  wire [5:0] not_1_out;

  assign not_1_out = ~opcode;  // NOT_Gate not_1, 6 bits wide
  assign not_2_out = ~func[4:2];  // NOT_Gate not_2, 3 bits wide
  and out_put (out_3, not_1_out[0], not_1_out[1], not_1_out[2], not_1_out[3], not_1_out[4], not_1_out[5], func[0], not_2_out[0], not_2_out[1], not_2_out[2], func[5]);
endmodule

module RegWrite_imp (
  input  [5:0] Opcode,
  input  [5:0] func,
  output out_3
);

  wire and_1_out, and_2_out, and_3_out;
  wire [1:0] not_4_out;
  wire [2:0] not_1_out, not_3_out;
  wire [5:0] not_2_out;

  assign not_1_out = ~Opcode[4:2];  // NOT_Gate not_1, 3 bits wide
  assign not_2_out = ~Opcode;  // NOT_Gate not_2, 6 bits wide
  assign not_3_out = ~func[4:2];  // NOT_Gate not_3, 3 bits wide
  assign not_4_out = ~Opcode[5:4];  // NOT_Gate not_4, 2 bits wide
  and and_1 (and_1_out, not_2_out[0], not_2_out[1], not_2_out[2], not_2_out[3], not_2_out[4], not_2_out[5], func[0], not_3_out[0], not_3_out[1], not_3_out[2], func[5]);
  and and_2 (and_2_out, Opcode[0], Opcode[2], Opcode[3], not_4_out[0], not_4_out[1]);
  and and_3 (and_3_out, Opcode[0], not_1_out[0], not_1_out[1], not_1_out[2], Opcode[5]);
  or or_1 (out_3, and_1_out, and_2_out, and_3_out);
endmodule

module ALUSrc_imp (
  input  [5:0] opcode,
  output out_2
);

  wire and_1_out, and_2_out, not_1_out, not_2_out, not_3_out, not_4_out;

  not not_1 (not_1_out, opcode[4]);
  not not_2 (not_2_out, opcode[5]);
  not not_3 (not_3_out, opcode[2]);
  not not_4 (not_4_out, opcode[4]);
  and and_1 (and_1_out, opcode[0], opcode[2], opcode[3], not_1_out, not_2_out);
  and and_2 (and_2_out, opcode[0], opcode[1], not_3_out, not_4_out, opcode[5]);
  or or_1 (out_2, and_1_out, and_2_out);

  // Notes on the sheet:
  //   这个是确定指令里面包不包含立即数
endmodule

module BEQ_imp (
  input  [5:0] opcode,
  output out_2
);

  wire not_1_out, not_2_out, not_3_out, not_4_out, not_5_out;

  not not_1 (not_1_out, opcode[0]);
  not not_2 (not_2_out, opcode[1]);
  not not_3 (not_3_out, opcode[3]);
  not not_4 (not_4_out, opcode[4]);
  not not_5 (not_5_out, opcode[5]);
  and and_1 (out_2, not_1_out, not_2_out, opcode[2], not_3_out, not_4_out, not_5_out);
endmodule

module MemWrite_imp (
  input  [5:0] opcode,
  output out_2
);

  wire not_1_out, not_2_out;

  not not_1 (not_1_out, opcode[2]);
  not not_2 (not_2_out, opcode[4]);
  and and_1 (out_2, opcode[0], opcode[1], not_1_out, opcode[3], not_2_out, opcode[5]);

  // Notes on the sheet:
  //   opcode: initial=0x2b
endmodule

module MemRead_imp (
  input  [5:0] opcode,
  output out_2
);

  wire not_1_out, not_2_out, not_3_out;

  not not_1 (not_1_out, opcode[2]);
  not not_2 (not_2_out, opcode[3]);
  not not_3 (not_3_out, opcode[4]);
  and and_1 (out_2, opcode[0], opcode[1], not_1_out, not_2_out, not_3_out, opcode[5]);

  // Notes on the sheet:
  //   opcode: initial=0x2b
endmodule

module Mem2Reg_imp (
  input  [5:0] opcode,
  output out_2
);

  wire not_1_out, not_2_out, not_3_out;

  not not_1 (not_1_out, opcode[2]);
  not not_2 (not_2_out, opcode[3]);
  not not_3 (not_3_out, opcode[4]);
  and and_1 (out_2, opcode[0], opcode[1], not_1_out, not_2_out, not_3_out, opcode[5]);

  // Notes on the sheet:
  //   opcode: initial=0x23
endmodule

module ExtOp_imp (
  input  [5:0] Opcode,
  output out_2
);

  wire not_1_out, not_2_out;

  not not_1 (not_1_out, Opcode[5]);
  not not_2 (not_2_out, Opcode[4]);
  and and_1 (out_2, not_1_out, not_2_out, Opcode[3], Opcode[2], Opcode[1], Opcode[0]);

  // Notes on the sheet:
  //   高位补0 还是 低位补0
endmodule

module ALUCtr0_imp (
  input  [5:0] Opcode,
  input  [5:0] func,
  output out_3
);

  wire add_out, lui_out, lw_out, not_2_out, not_3_out, not_4_out, not_5_out, not_6_out, not_7_out, not_8_out,
       not_9_out, not_10_out, not_11_out, not_12_out, not_13_out, not_14_out, not_15_out, ori_out, sw_out;
  wire [5:0] not_1_out;

  assign not_1_out = ~Opcode;  // NOT_Gate not_1, 6 bits wide
  not not_2 (not_2_out, func[1]);
  not not_3 (not_3_out, func[2]);
  not not_4 (not_4_out, func[3]);
  not not_5 (not_5_out, func[4]);
  not not_6 (not_6_out, Opcode[4]);
  not not_7 (not_7_out, Opcode[5]);
  not not_8 (not_8_out, Opcode[1]);
  not not_9 (not_9_out, Opcode[4]);
  not not_10 (not_10_out, Opcode[5]);
  not not_11 (not_11_out, Opcode[2]);
  not not_12 (not_12_out, Opcode[4]);
  not not_13 (not_13_out, Opcode[2]);
  not not_14 (not_14_out, Opcode[3]);
  not not_15 (not_15_out, Opcode[4]);
  and add (add_out, not_1_out[0], not_1_out[1], not_1_out[2], not_1_out[3], not_1_out[4], not_1_out[5], func[0], not_2_out, not_3_out, not_4_out, not_5_out, func[5]);
  and sw (sw_out, Opcode[0], Opcode[1], not_11_out, Opcode[3], not_12_out, Opcode[5]);
  and lw (lw_out, Opcode[0], Opcode[1], not_13_out, not_14_out, not_15_out, Opcode[5]);
  and lui (lui_out, Opcode[0], Opcode[1], Opcode[2], Opcode[3], not_6_out, not_7_out);
  and ori (ori_out, Opcode[0], not_8_out, Opcode[2], Opcode[3], not_9_out, not_10_out);
  or or_1 (out_3, add_out, sw_out, lw_out, lui_out, ori_out);
endmodule

module ALUCrt1_imp (
  input  [5:0] Opcode,
  output out_2
);

  wire not_1_out, not_2_out, not_3_out;

  not not_1 (not_1_out, Opcode[0]);
  not not_2 (not_2_out, Opcode[2]);
  not not_3 (not_3_out, Opcode[3]);
  or or_1 (out_2, not_1_out, Opcode[1], not_2_out, not_3_out, Opcode[4], Opcode[5]);
endmodule

module IsZero (
  input  [31:0] in_1,
  output out_2
);

  wire or_1_out;

  or or_1 (or_1_out, in_1[0], in_1[1], in_1[2], in_1[3], in_1[4], in_1[5], in_1[6], in_1[7], in_1[8], in_1[9], in_1[10], in_1[11], in_1[12], in_1[13], in_1[14], in_1[15], in_1[16], in_1[17], in_1[18], in_1[19], in_1[20], in_1[21], in_1[22], in_1[23], in_1[24], in_1[25], in_1[26], in_1[27], in_1[28], in_1[29], in_1[30], in_1[31]);
  not not_1 (out_2, or_1_out);
endmodule

module reg_4 (
  input  [31:0] in_1,
  input  read_or_write,
  input  clock,
  input  reset,
  input  [1:0] read_0,
  input  [1:0] read_1,
  input  [1:0] write_0,
  output [31:0] out_0,
  output [31:0] out_1
);

  wire decoder_1_out0, decoder_1_out1, decoder_1_out2, decoder_1_out3;
  wire [31:0] register_1_q, register_2_q, register_3_q, register_4_q;

  Decoder #(.select(2)) decoder_1 (
    .out0(decoder_1_out0), .out1(decoder_1_out1), .out2(decoder_1_out2), .out3(decoder_1_out3),
    .sel(write_0), .en(read_or_write));
  Register #(.width(32)) register_1 (.D(in_1), .en(decoder_1_out0), .clk(clock), .Q(register_1_q), .clr(reset));
  Register #(.width(32)) register_2 (.D(in_1), .en(decoder_1_out1), .clk(clock), .Q(register_2_q), .clr(reset));
  Register #(.width(32)) register_3 (.D(in_1), .en(decoder_1_out2), .clk(clock), .Q(register_3_q), .clr(reset));
  Register #(.width(32)) register_4 (.D(in_1), .en(decoder_1_out3), .clk(clock), .Q(register_4_q), .clr(reset));
  Multiplexer #(.select(2), .width(32)) multiplexer_1 (
    .in0(register_1_q), .in1(register_2_q), .in2(register_3_q), .in3(register_4_q), .out(out_1), .sel(read_1));
  Multiplexer #(.select(2), .width(32)) multiplexer_2 (
    .in0(register_1_q), .in1(register_2_q), .in2(register_3_q), .in3(register_4_q), .out(out_0), .sel(read_0));

  // Notes on the sheet:
  //   注意每一条之指令执行的时候r_w都会设置为相应的值
endmodule
